// Logisim project Programadores.circ as structural Verilog: 1 circuit, main circuit main
module main (
  input  in_1,
  input  in_2,
  input  in_3,
  input  in_4,
  input  in_5,
  input  in_6,
  input  in_7,
  input  in_8,
  input  in_9,
  input  in_10,
  input  in_11,
  input  in_12,
  input  in_13,
  input  in_14,
  input  in_15,
  input  in_16,
  input  in_17,
  input  in_18,
  input  in_19,
  input  in_20,
  input  in_21,
  input  in_22,
  input  in_23,
  input  in_24,
  input  in_25,
  input  in_26,
  input  in_27
);

  wire xor_1_out, xor_2_out, xor_3_out, xor_4_out, xor_5_out, xor_6_out, xor_7_out, xor_8_out, xor_9_out,
       xor_10_out, xor_11_out, xor_12_out, xor_13_out, xor_14_out, xor_15_out, xor_16_out, xor_17_out,
       xor_18_out, xor_19_out, xor_20_out, xor_21_out, xor_22_out, xor_23_out, xor_24_out, xor_25_out,
       xor_26_out, xor_27_out, xor_28_out, xor_29_out, xor_30_out, xor_31_out, xor_32_out, xor_33_out,
       xor_34_out;

  xor xor_1 (xor_1_out, in_1, in_2);
  xor xor_2 (xor_2_out, xor_1_out, in_3);
  xor xor_3 (xor_3_out, xor_2_out, in_4);
  xor xor_4 (xor_4_out, xor_3_out, in_5);
  xor xor_5 (xor_5_out, xor_4_out, in_6);
  xor xor_6 (xor_6_out, xor_5_out, in_7);
  xor xor_7 (xor_7_out, xor_6_out, in_8);
  xor xor_8 (xor_8_out, xor_7_out, in_25);
  LED led_1 (.in(xor_8_out));
  xor xor_9 (xor_9_out, xor_7_out, xor_17_out);
  xor xor_10 (xor_10_out, in_9, in_10);
  xor xor_11 (xor_11_out, xor_10_out, in_11);
  xor xor_12 (xor_12_out, xor_11_out, in_12);
  xor xor_13 (xor_13_out, xor_12_out, in_13);
  xor xor_14 (xor_14_out, xor_13_out, in_14);
  xor xor_15 (xor_15_out, xor_14_out, in_15);
  xor xor_16 (xor_16_out, xor_9_out, in_27);
  LED led_2 (.in(xor_16_out));
  xor xor_17 (xor_17_out, xor_15_out, in_16);
  xor xor_18 (xor_18_out, xor_17_out, in_26);
  LED led_3 (.in(xor_18_out));
  xor xor_19 (xor_19_out, in_1, in_9);
  xor xor_20 (xor_20_out, in_2, in_10);
  xor xor_21 (xor_21_out, in_3, in_11);
  xor xor_22 (xor_22_out, in_4, in_12);
  xor xor_23 (xor_23_out, in_5, in_13);
  xor xor_24 (xor_24_out, in_6, in_14);
  xor xor_25 (xor_25_out, in_7, in_15);
  xor xor_26 (xor_26_out, in_8, in_16);
  xor xor_27 (xor_27_out, xor_19_out, in_17);
  LED led_4 (.in(xor_27_out));
  LED led_5 (.in(xor_28_out));
  xor xor_28 (xor_28_out, xor_20_out, in_18);
  xor xor_29 (xor_29_out, xor_21_out, in_19);
  LED led_6 (.in(xor_29_out));
  LED led_7 (.in(xor_30_out));
  xor xor_30 (xor_30_out, xor_22_out, in_20);
  LED led_8 (.in(xor_31_out));
  xor xor_31 (xor_31_out, xor_23_out, in_21);
  xor xor_32 (xor_32_out, xor_24_out, in_22);
  LED led_9 (.in(xor_32_out));
  LED led_10 (.in(xor_33_out));
  xor xor_33 (xor_33_out, xor_25_out, in_23);
  LED led_11 (.in(xor_34_out));
  xor xor_34 (xor_34_out, xor_26_out, in_24);

  // Notes on the sheet:
  //   PARIDADE DA LINHA 1
  //   1° BYTE FORNECIDO PELO USUÁRIO
  //   PARIDADE DA LINHA 1
  //   PARIDADE DA LINHA 3
  //   PARIDADE DA LINHA 2
  //   2° BYTE FORNECIDO PELO USUÁRIO
  //   PARIDADE DA LINHA 3
  //   PARIDADE DA LINHA 2
  //   PARIDADES DAS COLUNAS
  //   1
  //   2
  //   3
  //   4
  //   5
  //   6
  //   7
  //   8
  //   3° BYTE FORNECIDO PELO USUÁRIO
  //   1
  //   2
  //   3
  //   4
  //   5
  //   6
  //   7
  //   8
  //   CHECAGEM DAS PARIDADES
  //   FORNECIDAS PELO USUÁRIO
  //   COM O SISTEMA
  //   OS LEDS SIMBOLIZAM A
  //   COLUNA QUE ESTÁ INCORRETA
  //   A PARIDADE FORNECIDA PELO
  //   USUÁRIO
endmodule
