// Logisim project Projeto1.circ as structural Verilog: 1 circuit, main circuit main
module main (
  input  A,
  input  B,
  input  C,
  input  D,
  input  P,
  output out_6,
  output out_7
);

  wire and_1_out, and_2_out, and_3_out, and_4_out, and_5_out, and_6_out, and_7_out, and_8_out, and_9_out,
       and_10_out, and_11_out, B_C_out, B_D_out, B_P_out, C_D_out, C_P_out, D_P_out, not_1_out, not_2_out,
       not_3_out, not_4_out, or_1_out, or_2_out, or_3_out, or_4_out;

  and C_P (C_P_out, C, P);
  and D_P (D_P_out, D, P);
  and C_D (C_D_out, C, D);
  and B_C (B_C_out, B, C);
  and B_P (B_P_out, B, P);
  and B_D (B_D_out, B, D);
  not not_1 (not_1_out, D);
  not not_2 (not_2_out, B);
  not not_3 (not_3_out, C);
  and and_1 (and_1_out, B_C_out, not_1_out);
  and and_2 (and_2_out, not_2_out, C_D_out);
  and and_3 (and_3_out, B, not_3_out, D);
  and and_4 (and_4_out, not_2_out, C, not_1_out);
  and and_5 (and_5_out, B, not_3_out, not_1_out);
  and and_6 (and_6_out, not_2_out, not_3_out, D);
  or or_1 (or_1_out, C_P_out, D_P_out, C_D_out);
  or or_2 (or_2_out, C_P_out, B_C_out, B_P_out, D_P_out, C_D_out);
  and and_7 (and_7_out, C, D, P);
  or or_3 (or_3_out, and_1_out, and_2_out, and_3_out);
  or or_4 (or_4_out, and_4_out, and_5_out, and_6_out);
  and and_8 (and_8_out, B, or_1_out);
  and and_9 (and_9_out, A, or_2_out);
  not not_4 (not_4_out, A);
  and and_10 (and_10_out, not_4_out, or_3_out);
  and and_11 (and_11_out, A, or_4_out);
  or or_5 (out_6, and_8_out, and_9_out, and_7_out);
  or or_6 (out_7, and_10_out, and_11_out);

  // Notes on the sheet:
  //   C^P
  //   D^P
  //   C^D
  //   (B^C)^~D
  //   ~B^(C^D)
  //   B^~C^D
  //   ~B^C^~D
  //   B^~C^~D
  //   ~B^~C^D
  //   ((C^P)v(D^P)v(C^P))
  //   ((B^C)v(C^P)v(B^P)v(D^P)v(C^D)v(B^D))
  //   (C^D^P)
  //   ((B^C)^~D)v(~B^(C^D)v(B^~C^D))
  //   ((~B^C^~D)v(B^~C^~D)v(~B^~C^D))
  //   B^((C^P)v(D^P)v(C^P))
  //   A^((B^C)v(C^P)v(B^P)v(D^P)v(C^D)v(B^D))
  //   ~A^((B^C)^~D)v(~B^(C^D)v(B^~C^D))
  //   A^((B^C)^~D)v(~B^(C^D)v(B^~C^D))
  //   Resultado
  //   Quem decidiu?
endmodule
