// Logisim project Projeto2.circ as structural Verilog: 1 circuit, main circuit main
module main (
  input  V1,
  input  V2,
  input  V3,
  input  V4,
  output V1SF,
  output nBvAvC,
  output V2SF,
  output V2SD,
  output nB_nD_vAvC,
  output nDvAvC,
  output V4SF,
  output V4SD
);

  wire and_1_out, and_2_out, and_3_out, and_4_out, and_5_out, and_6_out, and_7_out, and_8_out, and_9_out,
       and_10_out, and_11_out, not_1_out, not_2_out, not_3_out, not_4_out, not_5_out, not_6_out, not_7_out;

  not not_1 (not_1_out, V2);
  not not_2 (not_2_out, V4);
  not not_3 (not_3_out, V1);
  not not_4 (not_4_out, V3);
  not not_5 (not_5_out, V1);
  not not_6 (not_6_out, V3);
  and and_1 (and_1_out, not_1_out, not_2_out);
  and and_2 (and_2_out, not_3_out, V2, not_4_out);
  and and_3 (and_3_out, not_3_out, not_4_out, V4);
  and and_4 (and_4_out, V2, not_4_out);
  and and_5 (and_5_out, V1, not_4_out);
  and and_6 (and_6_out, not_4_out, V4, V4);
  and and_7 (and_7_out, not_5_out, V2, not_6_out);
  and and_8 (and_8_out, not_5_out, not_6_out, V4);
  and and_9 (and_9_out, not_5_out, V2);
  and and_10 (and_10_out, not_5_out, V4);
  and and_11 (and_11_out, not_5_out, V3);
  not not_7 (not_7_out, V4);
  or or_1 (V1SF, and_1_out, V1, V3);
  or or_2 (nBvAvC, not_1_out, V1, V3);
  or or_3 (V2SF, and_2_out, and_3_out);
  or or_4 (V2SD, and_4_out, and_5_out, and_6_out);
  or or_5 (nB_nD_vAvC, and_1_out, V1, V3);
  or or_6 (nDvAvC, not_7_out, V1, V3);
  or or_7 (V4SF, and_7_out, and_8_out);
  or or_8 (V4SD, and_9_out, and_10_out, and_11_out);

  // Notes on the sheet:
  //   A
  //   B
  //   C
  //   D
  //   ~B^~D
  //   ~A^B^~C
  //   ~A^~C^D
  //   B^~C
  //   A^~C
  //   ~C^D
  //   ~A^B^~C
  //   ~A^~C^D
  //   ~A^B
  //   ~A^D
  //   ~A^C
  //   A
  //   C
  //   V1SD
  //   V3SF
  //   V3SD
endmodule
