// Logisim project Projeto_circuito.circ as structural Verilog: 1 circuit, main circuit main
module main (
  input  in_1,
  input  in_2,
  input  in_3,
  input  in_4
);

  wire and_1_out, and_2_out, and_3_out, and_4_out, and_5_out, and_6_out, and_7_out, and_8_out, and_9_out,
       and_10_out, not_2_out, not_3_out, not_4_out, or_1_out, or_2_out, or_3_out, or_4_out, or_5_out,
       or_6_out, or_7_out;

  and and_1 (and_1_out, in_1, not_3_out);
  or or_1 (or_1_out, in_4, and_2_out, and_1_out, and_3_out, and_4_out);
  // NOT_Gate not_1 has open pins: in=in_4, out=open
  and and_2 (and_2_out, not_3_out, not_4_out);
  and and_3 (and_3_out, in_1, not_4_out);
  not not_2 (not_2_out, in_1);
  and and_4 (and_4_out, not_2_out, in_2, in_3);
  LED led_1 (.in(or_4_out));
  LED led_2 (.in(or_4_out));
  LED led_3 (.in(or_2_out));
  LED led_4 (.in(or_1_out));
  LED led_5 (.in(or_7_out));
  or or_2 (or_2_out, in_1, not_3_out, not_4_out);
  LED led_6 (.in(or_3_out));
  LED led_7 (.in(or_5_out));
  LED led_8 (.in(or_6_out));
  LED led_9 (.in(or_7_out));
  not not_3 (not_3_out, in_2);
  and and_5 (and_5_out, not_3_out, not_4_out);
  or or_3 (or_3_out, not_2_out, and_5_out);
  not not_4 (not_4_out, in_3);
  and and_6 (and_6_out, in_3, not_3_out);
  and and_7 (and_7_out, in_1, in_1, in_3);
  or or_4 (or_4_out, and_6_out, and_7_out, and_8_out);
  and and_8 (and_8_out, not_2_out, not_4_out);
  or or_5 (or_5_out, not_4_out, in_4);
  and and_9 (and_9_out, in_1, in_2);
  and and_10 (and_10_out, in_4, in_3);
  or or_6 (or_6_out, and_7_out, and_9_out, and_10_out);
  or or_7 (or_7_out, in_4, in_1, in_2, in_3);

  // Notes on the sheet:
  //   A
  //   B
  //   C
  //   D
endmodule
